# Fritzing sketch ESP_4CH (saved by Fritzing 0.9.3b)
circuit board: 7.95727cm x 4.39956cm
breadboards: 1

parts:
  R1 = Resistor [tolerance=±5% resistance=3.3k package=THT]
  R3 = Resistor [tolerance=±5% resistance=2k package=THT]
  U2 = Voltage Regulator - Variable [package="TO220 [THT]"]
  Part1 = Logic Level Converter [part_number="GPIO Voltage Converter"]
  J1 = Camdenboss CTB0158-2 [part_number=CTB0158-2 package=THT]
  J2 = Camdenboss CTB0158-6 [part_number=CTB0158-6 package=THT]
  R4 = Resistor [tolerance=±5% resistance=3.3k package=THT]
  R5 = Resistor [tolerance=±5% resistance=3.3k package=THT]
  U3 = ESP-12F (ESP8266 WiFi Module) [part_number=ESP8266]
  Q1 = Basic FET N-Channel [package="TO220 [THT]"]
  Q2 = Basic FET N-Channel [package="TO220 [THT]"]
  Q3 = Basic FET N-Channel [package="TO220 [THT]"]
  Q4 = Basic FET N-Channel [package="TO220 [THT]"]
  J7 = female pin header, 1 pin [form="♀ (female)"]
  J8 = female pin header, 1 pin [form="♀ (female)"]
  J9 = female pin header, 1 pin [form="♀ (female)"]
  J3 = male pin header, 5 pins [form="♂ (male)"]
  C1 = Electrolytic Capacitor [capacitance=400µF package="100 mil [THT, electrolytic]"]
  J6 = female pin header, 1 pin [form="♀ (female)"]

nets:
  GND: R1.Pin_0, Part1.GND, J1.pin1, R5.Pin_1, U3.GND, U3.GPIO15, Q1.source, Q2.source, Q3.source, Q4.source, J7.pin1, J8.pin1, J9.pin1, J3.pin5, C1.-, J6.pin1
  N1: R1.Pin_1, Part1.HV, R4.Pin_1
  N2: R3.Pin_0, U2.OUT, Part1.LV, U3.VCC, U3.GPIO2, U3.EN, J3.pin4
  N3: R3.Pin_1, U2.ADJ, R5.Pin_0
  12V: U2.IN, J1.pin2, J2.pin1, J2.pin2, R4.Pin_0, C1.+
  N4: Part1.TX2_LV, U3.GPIO14
  N5: Part1.RX2_LV, U3.GPIO12
  N6: Part1.RX_LV, U3.GPIO4
  N7: Part1.TX_LV, U3.GPIO5
  N8: Part1.TX_HV, Q4.gate
  N9: Part1.RX_HV, Q1.gate
  N10: Part1.RX2_HV, Q3.gate
  N11: Part1.TX2_HV, Q2.gate
  N12: J2.pin3, Q4.drain
  N13: J2.pin4, Q1.drain
  N14: J2.pin5, Q2.drain
  N15: J2.pin6, Q3.drain
  N16: U3.RXD0, J3.pin1
  N17: U3.GPIO0, J3.pin3
  N18: U3.TXD0, J3.pin2

notes:
  VER 1.0

custom parts:
  ESP-12F (ESP8266 WiFi Module): WiFi Module based on the ESP8266 with onboard PCB antenna and UART communications
